# Fritzing sketch PIR (saved by Fritzing 0.9.2b)

parts:
  PIR1 = PIR sensor
  Raspberry_Pi1 = Raspberry Pi 2

nets:
  VDD: PIR1.VDD, Raspberry_Pi1.5V
  N1: PIR1.SIG, Raspberry_Pi1.GPIO21
  N2: PIR1.GND, Raspberry_Pi1.GPIO14

// code stored in the sketch: Untitled2.bas
import RPi.GPIO as GPIO
import time
pir=11
led=12
GPIO.setmode(GPIO.BOARD)
GPIO.setup(pir,GPIO.IN)
GPIO.setup(led,GPIO.OUT)
while 1:
			if GPIO.input(pir):
	
						GPIO.output (led,GPIO.HIGH)
						print "Ti Vedo!"
						time.sleep (5)
			else:
			
						GPIO.output (led,GPIO.LOW)
						print "Non ti vedo"
						time.sleep (1)
